// Logisim project Arquitetura de Computadores Avaliação 1.circ as structural Verilog: 1 circuit, main circuit main
module main (
  input  in_1,
  input  in_2,
  input  in_3,
  input  in_4,
  input  in_5,
  input  in_6
);

  // somador_3bits_main main_1: pin names not known; wires that end beside it: in_1, in_2, in_3, in_4
endmodule
